// Digital circuit Digital_Counter.dig as structural Verilog
module Digital_Counter (
  input  C,
  input  en,
  input  [3:0] Max,
  output [3:0] Q,
  output wrap
);

  wire [3:0] add_1_s, multiplexer_1_out;

  Add #(.Bits(4)) add_1 (.a(Q), .b(4'b0001), .c_i(1'b0), .s(add_1_s));  // open: c_o
  Comparator #(.Bits(4)) comparator_1 (.a(Q), .b(Max), .eq(wrap));  // open: gt, lt
  Multiplexer #(.Bits(4)) multiplexer_1 (.sel(wrap), .in_0(add_1_s), .in_1(4'b0000), .out(multiplexer_1_out));
  Register #(.Bits(4)) register_1 (.D(multiplexer_1_out), .C(C), .en(en), .Q(Q));
  Seven_Seg_Hex seven_seg_hex_1 (.d(Q), .dp(1'b0));
endmodule
