// Digital circuit clock_main.dig as structural Verilog
module clock_main (
  input  clk
);

  wire and_1_out, and_2_out, digital_counter_1_wrap, digital_counter_2_wrap, digital_counter_3_wrap;
  wire [3:0] digital_counter_1_q, digital_counter_2_q, digital_counter_3_q, digital_counter_4_q;

  Seven_Seg_Hex seven_seg_hex_1 (.d(digital_counter_4_q), .dp(1'b0));
  Digital_Counter digital_counter_1 (
    .C(clk), .en(1'b1), .Max(4'b1001), .Q(digital_counter_1_q), .wrap(digital_counter_1_wrap));
  Seven_Seg_Hex seven_seg_hex_2 (.d(digital_counter_3_q), .dp(1'b0));
  Digital_Counter digital_counter_2 (
    .C(clk), .en(digital_counter_1_wrap), .Max(4'b0101), .Q(digital_counter_2_q),
    .wrap(digital_counter_2_wrap));
  and and_1 (and_1_out, digital_counter_1_wrap, digital_counter_2_wrap);
  Seven_Seg_Hex seven_seg_hex_3 (.d(digital_counter_2_q), .dp(1'b0));
  Digital_Counter digital_counter_3 (
    .C(clk), .en(and_1_out), .Max(4'b1001), .Q(digital_counter_3_q), .wrap(digital_counter_3_wrap));
  and and_2 (and_2_out, and_1_out, digital_counter_3_wrap);
  Digital_Counter digital_counter_4 (.C(clk), .en(and_2_out), .Max(4'b0101), .Q(digital_counter_4_q));  // open: wrap
  Seven_Seg_Hex seven_seg_hex_4 (.d(digital_counter_1_q), .dp(1'b0));

  // Notes on the sheet:
  //   clk: Hz: 10
endmodule
